# Fritzing sketch Schematic (saved by Fritzing 0.9.10b)
breadboards: 1

parts:
  M1 = Stepper Motor - Bipolar
  Pololu_A1 = Pololu A4988 [package=SO16]
  Pololu_A2 = Pololu A4988 [package=SO16]
  C1 = Electrolytic Capacitor [capacitance=1µF voltage=35V package="100 mil [THT, electrolytic]"]
  C2 = Electrolytic Capacitor [capacitance=1µF voltage=35V package="100 mil [THT, electrolytic]"]
  M2 = Stepper Motor - Bipolar
  Part1 = Arduino Uno (Rev3)
  VCC1 = 4 x AAA Battery Mount

nets:
  N1: M1.A, Pololu_A2.2B
  N2: M1.C, Pololu_A2.2A
  N3: M1.B, Pololu_A2.1A
  N4: M1.D, Pololu_A2.1B
  N5: Pololu_A1.RESET, Pololu_A1.SLEEP
  N6: Pololu_A1.STEP, Part1.D4
  N7: Pololu_A1.DIR, Part1.D3_PWM
  GND: Pololu_A1.GND, Pololu_A2.GND, C1.-, C2.-
  N8: Pololu_A1.1B, M2.D
  N9: Pololu_A1.1A, M2.B
  N10: Pololu_A1.2A, M2.C
  N11: Pololu_A1.2B, M2.A
  N12: Pololu_A1.VMOT, Pololu_A2.VMOT, C1.+, C2.+
  N13: Pololu_A2.RESET, Pololu_A2.SLEEP
  N14: Pololu_A2.STEP, Part1.D7
  N15: Pololu_A2.DIR, Part1.D6_PWM
  N16: Part1.GND, VCC1.-
  N17: Part1.VIN, VCC1.+
